# Fritzing sketch transistorAmplifier_bb (saved by Fritzing 0.9.3b)
breadboards: 1

parts:
  Q1 = NPN-Transistor [package="TO92 [THT]"]
  Q2 = NPN-Transistor [package="TO92 [THT]"]
  Q3 = NPN-Transistor [package="TO92 [THT]"]
  Q4 = NPN-Transistor [package="TO92 [THT]"]
  Q5 = PNP-Transistor [package="SOT-23 [SMD]"]
  TRRS1 = Audio Jack (TRRS) 3.5mm [part_number="LUMBERG JEITA RC-5325A" package="RC-5325A [SMD]"]
  BAT1 = Battery Holders [package=battcom_20mm_pth]
  ANT1 = Antenna

nets:
  N1: Q1.E, Q2.B
  N2: Q1.B, Q5.2
  N3: Q1.C, Q2.C, Q3.C, Q4.C, Q5.1, BAT1.+
  N4: Q2.E, Q3.B
  N5: Q3.E, Q4.B
  N6: Q4.E, TRRS1.SLEEVE, TRRS1.RING2
  N7: Q5.0, ANT1.antenna_lead
  N8: TRRS1.RING1, BAT1.-
